# Fritzing sketch sumeshi (saved by Fritzing 0.9.3b)
breadboards: 1

parts:
  パーツ1 = Arduino Uno (Rev3) - ICSP
  J1 = Piezo Speaker
  S1 = Pushbutton [package="[THT]"]
  LED1 = RGB LED PL9823 F5 [package="5 mm [THT]"]
  LED2 = RGB LED PL9823 F5 [package="5 mm [THT]"]
  LED3 = LED - 5mm [color="Red (633nm)" package="5 mm [THT]"]
  LED4 = LED - 5mm [color="Red (633nm)" package="5 mm [THT]"]
  DHT1 = DHT11 Humitidy and Temperature Sensor
  R3 = PHOTOCELL [package=photocell-kit]
  R4 = Resistor [tolerance=±5% resistance=220 package=THT]
  R5 = Resistor [tolerance=±5% resistance=220 package=THT]
  R6 = Resistor [tolerance=±5% resistance=220 package=THT]
  R7 = Resistor [tolerance=±5% resistance=220 package=THT]
  R8 = Resistor [tolerance=±5% resistance=220 package=THT]

nets:
  N1: パーツ1.A0, R3.P$1
  N2: パーツ1.D9_PWM, R5.Pin_1
  N3: パーツ1.D10_PWM/SS, R6.Pin_1
  N4: パーツ1.D12/MISO, LED3.anode
  N5: パーツ1.D13/SCK, LED4.anode
  N6: パーツ1.D5_PWM, R4.Pin_1
  N7: パーツ1.D6_PWM, J1.pin2
  N8: パーツ1.D7, DHT1.NULL
  N9: パーツ1.5V, DHT1.DATA
  GND: パーツ1.GND, J1.pin1, S1.Pin_1, S1.Pin_2, LED1.GND, LED2.GND, DHT1.GND, R3.P$2, R7.Pin_1, R8.Pin_1
  N10: S1.Pin_3, S1.Pin_4
  N11: LED1.DO, LED2.DO, R4.Pin_0
  VDD: LED1.VDD, LED2.VDD, R5.Pin_0
  N12: LED1.DIN, LED2.DIN, R6.Pin_0
  N13: LED3.cathode, R7.Pin_0
  N14: LED4.cathode, R8.Pin_0

custom parts:
  RGB LED PL9823 F5: A 5mm tri-color LED with red, green and blue inside. this led includes WS2811 controller.
  DHT11 Humitidy and Temperature Sensor: DHT11 Humidity and Temperature Sensor
